// Digital circuit addressSpace.dig as structural Verilog
module addressSpace (
  input  [15:0] IA,
  input  [15:0] DA,
  input  [15:0] Din,
  input  str,
  input  C,
  output I,
  output D
);

  wire and_1_out, Data_d, Program_d;
  wire [15:0] RAM_d1, RAM_d2;

  and and_1 (and_1_out, str, DA[13]);
  ROM Program (.A(IA[1:0]), .sel(1'b1), .D(Program_d));
  ROM Data (.A(DA[1:0]), .sel(1'b1), .D(Data_d));
  RAMDualAccess #(.AddrBits(13), .Bits(16)) RAM (
    .str(and_1_out), .C(C), .ld(1'b1), .A1(DA[12:0]), .Din1(Din), .A2(IA[12:0]), .D1(RAM_d1), .D2(RAM_d2));
  Multiplexer multiplexer_1 (.in_0(Program_d), .in_1(RAM_d2[0]));  // open: sel, out
  Multiplexer multiplexer_2 (.in_0(Data_d), .in_1(RAM_d1[0]));  // open: sel, out
  // Pins of 1 and 2 and 13 and 16 bits meet at DA
  // Pins of 1 and 16 bits meet at Din
  // Pins of 1 and 2 and 13 and 16 bits meet at IA
  // Pins of 1 and 16 bits meet at RAM_d1
  // Pins of 1 and 16 bits meet at RAM_d2

  // Other names for the same wires on the sheet: Data_High = DA[13]; Inst_High = IA[13]
endmodule
