// Digital circuit alu.dig as structural Verilog
module alu (
  input  [15:0] a,
  input  [15:0] b,
  input  [3:0] op,
  input  C,
  output [15:0] out,
  output [16:0] cry
);

  wire multiplexer_1_out, Write_Carry_d, xor_2_out;
  wire [0:0] add_1_c_o;
  wire [15:0] add_1_s, and_1_out, bitextender_1_out, bitextender_2_out, \cₒ , or_1_out, \shiftleft_1_cₒ ,
       shiftleft_1_out, shiftright_1_p4, shiftright_1_p5, xor_1_out, xor_3_out;
  wire [16:0] \cᵢ ;
  wire [31:0] mul_1_mul;
  wire [31:16] undriven;

  BitExtender #(.inputBits(1)) bitextender_1 (.in(op[0]), .out(bitextender_1_out));
  BitExtender #(.inputBits(1)) bitextender_2 (.in(a[15]), .out(bitextender_2_out));
  assign xor_1_out = a ^ bitextender_1_out;  // XOr xor_1, 16 bits wide
  xor xor_2 (xor_2_out, \cᵢ [0], op[0]);
  ROM #(.AddrBits(3)) Write_Carry (.A(op[2:0]), .sel(1'b1), .D(Write_Carry_d));
  Multiplexer multiplexer_1 (.sel(op[3]), .in_0(bitextender_2_out[0]), .in_1(\cᵢ [0]), .out(multiplexer_1_out));
  shiftLeft shiftleft_1 (.in(a), .fill(\cᵢ [15:0]), .shift(b[3:0]), .out(shiftleft_1_out), .\cₒ (\shiftleft_1_cₒ ));
  // shiftRight shiftright_1: pin names not known; wires that end beside it: a, multiplexer_1_out, b[3:0], shiftright_1_p4, shiftright_1_p5
  Add #(.Bits(16)) add_1 (.a(xor_1_out), .b(b), .c_i(xor_2_out), .s(add_1_s), .c_o(add_1_c_o[0]));
  Mul #(.Signed("true"), .Bits(16)) mul_1 (.a(a), .b(b), .mul(mul_1_mul));
  Register #(.Bits(16)) Carry (.D(\cₒ ), .C(C), .en(Write_Carry_d), .Q(cry[15:0]));
  assign or_1_out = a | b;  // Or or_1, 16 bits wide
  assign and_1_out = a & b;  // And and_1, 16 bits wide
  assign xor_3_out = a ^ b;  // XOr xor_3, 16 bits wide
  Multiplexer #(.Bits(17)) multiplexer_2 (.sel(op[3]), .in_0({17{1'b0}}), .in_1(cry), .out(\cᵢ ));
  Multiplexer #(.Selector_Bits(3), .Bits(16)) multiplexer_3 (
    .sel(op[2:0]), .in_0({{15{1'b0}}, add_1_c_o[0]}), .in_1({{15{1'b0}}, add_1_c_o[0]}),
    .in_2(\shiftleft_1_cₒ ), .in_3(shiftright_1_p5), .in_4(mul_1_mul[31:16]), .in_5({16{1'b0}}),
    .in_6({16{1'b0}}), .in_7({16{1'b0}}), .out(\cₒ ));
  Multiplexer #(.Selector_Bits(3), .Bits(16)) multiplexer_4 (
    .sel(op[2:0]), .in_0(add_1_s), .in_1(add_1_s), .in_2(shiftleft_1_out), .in_3(shiftright_1_p4),
    .in_4(mul_1_mul[15:0]), .in_5(or_1_out), .in_6(and_1_out), .in_7(xor_3_out), .out(out));
  // Pins of 16 and 17 bits meet at cry
  // Pins of 1 and 16 and 17 bits meet at \cᵢ 
  // Pins of 16 and 32 bits meet at {undriven, xor_1_out}
  // Pins of 16 and 17 bits meet at {1'b0, \shiftleft_1_cₒ }
  // Pins of 16 and 17 bits meet at {1'b0, shiftright_1_p5}
  // Pins of 1 and 16 bits meet at bitextender_2_out

  // Other names for the same wires on the sheet: fun3[2:0] = op[2:0]; sub = op[0]; carry = op[3]

  // Notes on the sheet:
  //   Control
  //   Addition & Subtraction
  //   Shifting
  //   contents of Write_Carry (hex, n*v repeats v):
  //   5*1
  //   Multiplication
  //   Bitwise Logic
endmodule
