// Digital circuit canis.dig as structural Verilog
module canis (
  input  clk
);

  wire and_1_out, comparator_1_out, decoder_1_alubs, decoder_1_jmp, decoder_1_str, decoder_1_we;
  wire [1:0] decoder_1_aluas, decoder_1_dsrc;
  wire [2:0] decoder_1_cmpo, decoder_1_ra, decoder_1_rb, decoder_1_rw;
  wire [3:0] decoder_1_aluo;
  wire [15:0] add_1_s, addressspace_1_d, addressspace_1_i, alu_1_out, decoder_1_imm, multiplexer_1_out,
       multiplexer_2_out, multiplexer_3_out, multiplexer_4_out, PC_q, Registers_da, Registers_db;

  Register #(.Bits(16), .generic("this.Bits=int(args.bits);")) PC (.D(multiplexer_1_out), .C(clk), .en(1'b1), .Q(PC_q));
  Add #(.Bits(16)) add_1 (.a(PC_q), .b(16'h1), .c_i(1'b0), .s(add_1_s));  // open: c_o
  comparator comparator_1 (.val(Registers_da), .op(decoder_1_cmpo), .out(comparator_1_out));
  and and_1 (and_1_out, comparator_1_out, decoder_1_jmp);
  Multiplexer #(.Bits(16)) multiplexer_1 (.sel(and_1_out), .in_0(add_1_s), .in_1(alu_1_out), .out(multiplexer_1_out));
  addressSpace addressspace_1 (
    .C(clk), .Ia(PC_q), .Da(alu_1_out), .Din(Registers_db), .str(decoder_1_str), .I(addressspace_1_i),
    .D(addressspace_1_d));
  decoder decoder_1 (
    .C(clk), .I(addressspace_1_i), .imm(decoder_1_imm), .ALUaS(decoder_1_aluas), .ALUbS(decoder_1_alubs),
    .ALUo(decoder_1_aluo), .Dsrc(decoder_1_dsrc), .we(decoder_1_we), .Rw(decoder_1_rw), .Ra(decoder_1_ra),
    .Rb(decoder_1_rb), .str(decoder_1_str), .jmp(decoder_1_jmp), .CmpO(decoder_1_cmpo));
  Multiplexer #(.Selector_Bits(2), .Bits(16)) multiplexer_2 (
    .sel(decoder_1_dsrc), .in_0(alu_1_out), .in_1(addressspace_1_d), .in_2(add_1_s), .in_3({16{1'b0}}),
    .out(multiplexer_2_out));
  RegisterFile #(.AddrBits(3), .Bits(16)) Registers (
    .Din(multiplexer_2_out), .we(decoder_1_we), .Rw(decoder_1_rw), .C(clk), .Ra(decoder_1_ra),
    .Rb(decoder_1_rb), .Da(Registers_da), .Db(Registers_db));
  Multiplexer #(.Selector_Bits(2), .Bits(16)) multiplexer_3 (
    .sel(decoder_1_aluas), .in_0(Registers_da), .in_1(add_1_s), .in_2({16{1'b0}}), .in_3({16{1'b0}}),
    .out(multiplexer_3_out));
  Multiplexer #(.Bits(16)) multiplexer_4 (
    .sel(decoder_1_alubs), .in_0(Registers_db), .in_1(decoder_1_imm), .out(multiplexer_4_out));
  alu alu_1 (.C(clk), .a(multiplexer_3_out), .b(multiplexer_4_out), .op(decoder_1_aluo), .out(alu_1_out));
endmodule
