// Digital circuit decoder.dig as structural Verilog
module decoder (
  input  C,
  input  [15:0] I,
  output [15:0] imm,
  output [1:0] ALUaS,
  output ALUbS,
  output [3:0] ALUo,
  output [1:0] Dsrc,
  output we,
  output [2:0] Rw,
  output [2:0] Ra,
  output [2:0] Rb,
  output str,
  output jmp,
  output [2:0] CmpO
);

  wire and_1_out, conditional_jump, imm_2_0__select, imm_5_3__select, use_fun3_as_ALUo, write_to_rs1;
  wire [1:0] imm_size;
  wire [2:0] default_ALUo, fun3, multiplexer_2_out, rd;
  wire [3:0] etypebuffer_1_iext;
  wire [4:0] multiplexer_1_out;
  wire [5:3] multiplexer_3_out;
  wire [15:0] bitextender_1_out, bitextender_2_out, bitextender_3_out;
  wire [19:19] OpcodeLUT_d;
  wire [31:16] etypebuffer_1_iext_2;

  eTypeBuffer etypebuffer_1 (.I(I), .C(C), .Iext({etypebuffer_1_iext_2, Ra, fun3, Rb, rd, etypebuffer_1_iext}));
  and and_1 (and_1_out, etypebuffer_1_iext[3], etypebuffer_1_iext[2], etypebuffer_1_iext[1], etypebuffer_1_iext[0]);
  Multiplexer #(.Bits(5)) multiplexer_1 (
    .sel(and_1_out), .in_0({1'b0, etypebuffer_1_iext}), .in_1({2'b10, Ra}), .out(multiplexer_1_out));
  ROM #(.AddrBits(5), .Bits(20)) OpcodeLUT (
    .A(multiplexer_1_out), .sel(1'b1),
    .D({OpcodeLUT_d[19], conditional_jump, jmp, str, write_to_rs1, we, Dsrc, ALUaS, ALUbS, ALUo[3], use_fun3_as_ALUo, default_ALUo, imm_size, imm_5_3__select, imm_2_0__select}));
  Multiplexer #(.Bits(3)) multiplexer_2 (.sel(imm_2_0__select), .in_0(rd), .in_1(Rb), .out(multiplexer_2_out));
  Multiplexer #(.Bits(3)) multiplexer_3 (.sel(imm_5_3__select), .in_0(Rb), .in_1(fun3), .out(multiplexer_3_out));
  BitExtender #(.inputBits(3)) bitextender_1 (.in(multiplexer_2_out), .out(bitextender_1_out));
  BitExtender #(.inputBits(6)) bitextender_2 (.in({multiplexer_3_out, multiplexer_2_out}), .out(bitextender_2_out));
  BitExtender #(.inputBits(9)) bitextender_3 (.in({Ra, multiplexer_3_out, multiplexer_2_out}), .out(bitextender_3_out));
  Multiplexer #(.Selector_Bits(2), .Bits(16)) multiplexer_4 (
    .sel(imm_size), .in_0(bitextender_1_out), .in_1(bitextender_2_out), .in_2(bitextender_3_out),
    .in_3(etypebuffer_1_iext_2), .out(imm));
  Multiplexer #(.Bits(3)) multiplexer_5 (.sel(write_to_rs1), .in_0(rd), .in_1(Ra), .out(Rw));
  Multiplexer #(.Bits(3)) multiplexer_6 (.sel(conditional_jump), .in_0(3'b111), .in_1(fun3), .out(CmpO));
  Multiplexer #(.Bits(3)) multiplexer_7 (.sel(use_fun3_as_ALUo), .in_0(default_ALUo), .in_1(fun3), .out(ALUo[2:0]));

  // Other names for the same wires on the sheet: ALU_carry = ALUo[3]; ALUb_use_imm = ALUbS; ALUa_source[1:0] = ALUaS;
  //   write_register_source[1:0] = Dsrc; enable_register_write = we; enable_memory_write = str; enable_jump = jmp;
  //   rs2[2:0] = Rb; rs1[2:0] = Ra; clock = C

  // Notes on the sheet:
  //   OpcodeLUT bit format
  //   0 -> Read imm[2:0] from instr[9:7], else from instr[6:4]
  //   1 -> Read imm[5:3] from instr[12:10], else from instr[9:7]
  //   2-3 -> 0: Extend imm from 3 bits, 1: Extend imm from 6 bits, 2: Extend imm from 9 bits, 3: Use instr[31:15] as imm
  //   4-6 -> Default ALUo
  //   7 -> Use fun3 as ALUo, else default
  //   8 -> Enable ALU carry
  //   9 -> Use immediate as ALUb, else rs2
  //   10-11 -> ALUa value: 0: rs1, 1: PC, 3: zero
  //   12-13 -> Register data 0: ALU, 1: Memory, 2: Next PC, 3: Timer
  //   14 -> Enable register write
  //   15 -> Write to rs1, else rd
  //   16 -> Enable memory write
  //   17 -> Enable jump
  //   18 -> Condition jump on fun3, otherwise always
  //   opcd fn3 T     16   12   8    4    0  ctrlhex
  //                  v    v    v    v    v
  //   0000     R  0000 0100 0000 1000 0000  0x04080
  //   0001     R  0000 0100 0001 1000 0000  0x04180
  //   0010     I  0000 0100 0010 1000 0001  0x04281
  //   0011     B  0000 1100 0010 1000 0100  0x0C284
  //   0100     E  0000 0100 0010 1000 1100  0x0428C
  //   0101     J  0000 0100 1110 0000 1011  0x04E0B
  //   0110     E  0000 0100 1110 0000 1100  0x04E0C
  //   0111     L  0000 0101 0010 0100 0111  0x05247
  //   1000     S  0001 0000 0010 0100 0110  0x10246
  //   1001     B  0110 0000 0110 0100 0001  0x50601
  //   1010     J  0010 0000 0110 0100 1011  0x1060B
  //   1011     I  0010 0000 0010 0100 0001  0x10241
  //   1100     J  0010 0110 0110 0100 1011  0x1660B
  //   1101     E  0010 0110 0010 0000 1100  0x1620C
  //   1110     I  0000 0000 0000 0000 0001  0x00001
  //   ---------------------------------------------
  //   1111 000 I  0000 0000 0000 0000 0001  0x00001
  //   1111 001 I  0000 0000 0000 0000 0001  0x00001
  //   1111 010 I  0000 0000 0000 0000 0001  0x00001
  //   1111 011 I  0000 0000 0000 0000 0001  0x00001
  //   1111 100 I  0000 0000 0000 0000 0001  0x00001
  //   1111 110 I  0000 0000 0000 0000 0001  0x00001
  //   1111 111 I  0000 0000 0000 0000 0001  0x00001
  //   contents of OpcodeLUT (hex, n*v repeats v):
  //   4080,4180,4281,c284,428c,4e0b,4e0c,5247,10246,50601,1060b,10241
  //   ,1660b,1620c
endmodule
